# Fritzing sketch SPACEAPPSMODEL (saved by Fritzing 0.9.3b)
breadboards: 1

parts:
  Part1 = MQ-4
  A1 = MG881 CO2 Sensor
  M1 = RioRand LM2596
  esp1 = ESP32 DevKitc V4
  M2 = RioRand LM2596
  M3 = RioRand LM2596
  BAT1 = BC9VPC [package=bc9vpc]
  S1 = Round Pushbutton
  R1 = Resistor [tolerance=±5% resistance=470 package="0402 [SMD]"]
  LED1 = LEDs [package=led10mm]

nets:
  N1: Part1.VCC, M2.Pin_3
  N2: Part1.GND, M2.Pin_4
  N3: Part1.AO, esp1.IO0
  N4: A1.Pin_1, esp1.IO2
  N5: A1.Pin_2, M3.Pin_3
  N6: A1.Pin_3, M3.Pin_4
  N7: M1.Pin_1, M2.Pin_1, M3.Pin_1, BAT1.V+, S1.leg0, R1.Pin_1
  N8: M1.Pin_2, M2.Pin_2, M3.Pin_2, BAT1.V-, S1.leg1, LED1.A
  N9: M1.Pin_3, esp1.3V3
  N10: M1.Pin_4, esp1.GND
  N11: R1.Pin_0, LED1.C

custom parts:
  MG881 CO2 Sensor: This is the first CO2 sensor in the Arduino market. The output voltage of the module falls as the concentration of the CO2 increases.
  ESP32 DevKitc V4: ESP32-DevKitC board with ESP32-WROOM-32 module. ESP32-DevKitC V4 is a small-sized ESP32-based development board produced by Espressif. Most of the pins on the ESP module are broken out to the pin headers on the board. The pins D0, D1, D2, D3, CMD and CLK are used internally for communication between ESP32 and SPI flash memory. They are grouped on both sides near the USB connector. Avoid using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
